# Fritzing sketch Lunex (saved by Fritzing 0.9.3b)

parts:
  Raspberry_Pi_1 = Raspberry Pi 3 [part_number=RPI-3-V1.2]
  Composant1 = Arduino Uno (Rev3)
  J1 = Basic Servo
  hc-sr2 = hc-sr04

nets:
  GND: Raspberry_Pi_1.GND, Composant1.GND, J1.gnd, hc-sr2.GND
  5V: Raspberry_Pi_1.5V, Composant1.VIN
  N1: Composant1.D11_PWM/MOSI, hc-sr2.Echo
  N2: Composant1.D12/MISO, hc-sr2.Trig
  N3: Composant1.D5_PWM, J1.pulse
  VCC: Composant1.5V, J1.vcc, hc-sr2.VCC

custom parts:
  hc-sr04: This is a HC-SR04 Distance Sensor
